// Logisim project ex4-test.circ as structural Verilog: 1 circuit, main circuit main
module main (
  output halt,
  output [2:0] CYCLE,
  output FSM_IN,
  output FSM_OUT
);

  wire clock_1_out;
  wire [2:0] adder_1_out;

  Comparator #(.width(3)) comparator_1 (.a(3'b111), .b(CYCLE), .eq(halt));  // open: gt, lt
  Register #(.width(3)) register_1 (.D(adder_1_out), .clk(clock_1_out), .Q(CYCLE));  // open: en, clr
  Adder #(.width(3)) adder_1 (.a(CYCLE), .b(3'b001), .out(adder_1_out));  // open: cin, cout
  Clock clock_1 (.out(clock_1_out));
  ROM #(.addrWidth(3), .dataWidth(1)) rom_1 (.addr(CYCLE));  // open: data
  FSM fsm_1 (.INPUT0(FSM_IN), .OUTPUT0(FSM_OUT));

  // Notes on the sheet:
  //   contents of rom_1 (hex, n*v repeats v):
  //   0 1 0 1 1 0 1
endmodule
