// Logisim project ex2-test.circ as structural Verilog: 1 circuit, main circuit main
module main (
  output halt,
  output [7:0] OUT1,
  output [7:0] CYCLE
);

  wire CLK;
  wire [7:0] adder_1_out, Address_Counter_q, INPUT1;

  Clock u_CLK (.out(CLK));
  Comparator #(.mode("unsigned")) comparator_1 (.a(8'hfe), .b(CYCLE), .eq(halt));  // open: gt, lt
  Register register_1 (.D(adder_1_out), .clk(CLK), .Q(CYCLE));  // open: en, clr
  Adder adder_1 (.a(CYCLE), .b(8'h1), .out(adder_1_out));  // open: cin, cout
  Counter Address_Counter (.clk(CLK), .Q(Address_Counter_q));  // open: clr, load, up, count, D, carry
  ROM rom_1 (.addr(Address_Counter_q), .data(INPUT1));
  pipelined pipelined_1 (.in1(INPUT1), .in2(INPUT1), .CLK(CLK), .out1(OUT1));

  // Other names for the same wires on the sheet: INPUT2[7:0] = INPUT1

  // Notes on the sheet:
  //   contents of rom_1 (hex, n*v repeats v):
  //   3 2 fc 1 2 fb 1
endmodule
